// Logisim project Lavavajilla_final.circ as structural Verilog: 4 circuits, main circuit main
module main (
  input  Puerta,
  input  Start,
  input  M1,
  input  M0,
  input  A,
  output LAVO,
  output BOMBA_ABRILLANTADOR
);

  wire and_1_out, and_3_out, and_4_out, and_5_out, and_6_out, and_7_out, and_8_out, and_9_out, clock_1_out,
       D0_out, D1_out, D2_out, display_1_a, display_1_b, display_1_c, display_1_d, display_1_e, display_1_f,
       display_1_g, DONE_2, DONE_4, nDONE_2, nDONE_4, nM0, nM1, not_1_out, nQ0, nQ1, nQ2, nS, or_1_out,
       or_2_out, or_3_out, or_4_out, or_5_out, Q0, Q1, Q2, T1_out, T2_out, T3_out, T4_out, T5_out, T6_out,
       T7_out;

  Clock clock_1 (.out(clock_1_out));
  not not_1 (not_1_out, Puerta);
  D_Flip_Flop u_Q2 (.D(D2_out), .clk(clock_1_out), .Q(Q2), .Qn(nQ2), .reset(not_1_out));  // open: preset
  D_Flip_Flop u_Q1 (.D(D1_out), .clk(clock_1_out), .Q(Q1), .Qn(nQ1), .reset(not_1_out));  // open: preset
  D_Flip_Flop u_Q0 (.D(D0_out), .clk(clock_1_out), .Q(Q0), .Qn(nQ0), .reset(not_1_out));  // open: preset
  and and_1 (and_1_out, nM1, nM0);
  and and_2 (LAVO, Q2, nQ1, Q0);
  and and_3 (and_3_out, Q2, nQ1, nQ0);
  and and_4 (and_4_out, nQ2, Q1);
  Contador_2 contador_2_1 (.Clk(clock_1_out), .Enable(and_3_out), .Reset(not_1_out), .Done_2(DONE_2));
  Contador_4 contador_4_1 (.Clk(clock_1_out), .Enable(and_4_out), .Reset(not_1_out), .Done_4(DONE_4));
  or or_1 (or_1_out, nS, and_1_out);
  or or_2 (or_2_out, M1, M0);
  and T2 (T2_out, nQ2, nQ1, Q0, or_1_out);
  and T1 (T1_out, nQ2, nQ1, or_2_out, nQ0, Start);
  and T6 (T6_out, DONE_2, nQ0, Q2, nQ1);
  and T7 (T7_out, DONE_4, nQ2, Q1, Q0);
  not not_2 (nS, Start);
  not not_3 (nM0, M0);
  not not_4 (nDONE_4, DONE_4);
  not not_5 (nDONE_2, DONE_2);
  and and_5 (and_5_out, nQ2, nQ1, Q0, Start, M1, nM0);
  and and_6 (and_6_out, Q2, nQ1, nQ0);
  and and_7 (and_7_out, DONE_4, Q1, nQ2);
  and and_8 (and_8_out, nQ2, nQ1, Q0, Start, M0);
  and and_9 (and_9_out, nDONE_4, Q1, nQ2);
  and T3 (T3_out, M1, nQ2, nQ1, Q0, Start, M0);
  and T4 (T4_out, nDONE_4, Q0, Q1, nQ2);
  and T5 (T5_out, DONE_4, nQ0, Q1, nQ2);
  and and_10 (BOMBA_ABRILLANTADOR, A, and_4_out);
  or or_3 (or_3_out, and_8_out, and_9_out);
  or or_4 (or_4_out, and_5_out, and_6_out, and_7_out);
  not not_6 (nM1, M1);
  and D1 (D1_out, Puerta, or_3_out);
  DISPLAY display_1 (
    .Q2(Q2), .Q1(Q1), .Q0(Q0), .A(display_1_a), .B(display_1_b), .C(display_1_c), .D(display_1_d),
    .E(display_1_e), .F(display_1_f), .G(display_1_g));
  and D2 (D2_out, Puerta, or_4_out);
  or or_5 (or_5_out, T1_out, T2_out, T3_out, T4_out, T5_out, T6_out, T7_out);
  _7_Segment_Display u_7_segment_display_1 (
    .g(display_1_g), .f(display_1_f), .a(display_1_a), .b(display_1_b), .e(display_1_e), .d(display_1_d),
    .c(display_1_c));  // open: dp
  and D0 (D0_out, Puerta, or_5_out);

  // Other names for the same wires on the sheet: P = Puerta; S = Start

  // Notes on the sheet:
  //   S0 = Estado Inicial 
  //   S2 = ECO (01)
  //   S3 = INT (11)
  //   S4= Rapido (10) 
  //   S5 = Done
  //   S1 = Configuracion (Selector de modo)
endmodule

module Contador_4 (
  input  Clk,
  input  Enable,
  input  Reset,
  output Done_4
);

  wire C0_q, C0_qn, C1_q, multiplexer_1_out, multiplexer_2_out, xor_1_out;

  D_Flip_Flop C1 (.D(multiplexer_2_out), .clk(Clk), .Q(C1_q), .reset(Reset));  // open: Qn, preset
  D_Flip_Flop C0 (.D(multiplexer_1_out), .clk(Clk), .Q(C0_q), .Qn(C0_qn), .reset(Reset));  // open: preset
  xor xor_1 (xor_1_out, C1_q, C0_q);
  Multiplexer multiplexer_1 (.in0(C0_q), .in1(C0_qn), .out(multiplexer_1_out), .sel(Enable));
  Multiplexer multiplexer_2 (.in0(C1_q), .in1(xor_1_out), .out(multiplexer_2_out), .sel(Enable));
  and and_1 (Done_4, C1_q, C0_q);
endmodule

module Contador_2 (
  input  Clk,
  input  Enable,
  input  Reset,
  output Done_2
);

  wire d_ff_1_qn, multiplexer_1_out;

  D_Flip_Flop d_ff_1 (.D(multiplexer_1_out), .clk(Clk), .Q(Done_2), .Qn(d_ff_1_qn), .reset(Reset));  // open: preset
  Multiplexer multiplexer_1 (.in0(Done_2), .in1(d_ff_1_qn), .out(multiplexer_1_out), .sel(Enable));
endmodule

module DISPLAY (
  input  Q2,
  input  Q1,
  input  Q0,
  output A,
  output B,
  output C,
  output D,
  output E,
  output F,
  output G
);

  wire and_1_out, and_2_out, and_3_out, and_4_out, and_6_out, not_1_out, not_2_out, not_3_out;

  not not_1 (not_1_out, Q2);
  not not_2 (not_2_out, Q1);
  not not_3 (not_3_out, Q0);
  and and_1 (and_1_out, not_1_out, not_3_out);
  and and_2 (and_2_out, Q2, Q0);
  or or_1 (B, not_1_out, not_3_out);
  or or_2 (C, not_2_out, Q0);
  and and_3 (and_3_out, not_1_out, not_3_out);
  and and_4 (and_4_out, Q2, Q0);
  and and_5 (E, not_1_out, not_3_out);
  and and_6 (and_6_out, not_2_out, not_3_out);
  or or_3 (G, Q1, Q2);
  or or_4 (A, and_1_out, Q1, and_2_out);
  or or_5 (D, and_3_out, Q1, and_4_out);
  or or_6 (F, and_6_out, Q2);
endmodule
